# Fritzing sketch AetherOneSchematics (saved by Fritzing 0.9.3b)
circuit board: 8.46667cm x 5.64444cm
breadboards: 1

parts:
  Bauteil1 = Arduino Mega ADK (Rev3)
  R1 = Resistor [tolerance=±5% resistance=220 package=THT]
  LED1 = LED - 5mm [color="Infrared (850nm)" package="5 mm [THT]"]
  LED2 = LED - 5mm [color="Red (633nm)" package="5 mm [THT]"]
  LED3 = LED - 5mm [color="Green (555nm)" package="5 mm [THT]"]
  LED4 = LED - 5mm [color="Blue (430nm)" package="5 mm [THT]"]
  LED5 = LED - 5mm [color="White (4500K)" package="5 mm [THT]"]
  LED6 = LED - 5mm [color="Infrared (940nm)" package="5 mm [THT]"]
  L1 = Inductor [package="400 mil [THT]"]
  ANT1 = Antenna

nets:
  N1: Bauteil1.D24, LED1.anode
  N2: Bauteil1.D26, L1.pin_0, ANT1.antenna_lead
  N3: Bauteil1.D27, LED4.anode
  N4: Bauteil1.D28, LED2.anode
  N5: Bauteil1.D29, LED5.anode
  N6: Bauteil1.D30, LED3.anode
  N7: Bauteil1.D31, LED6.anode
  N8: Bauteil1.GND, R1.Pin_0
  N9: R1.Pin_1, LED1.cathode, LED2.cathode, LED3.cathode, LED4.cathode, LED5.cathode, LED6.cathode, L1.pin_1
