# Fritzing sketch ArduinoUnoAndAetherOneSchematics_2boardsCombined (saved by Fritzing 0.9.3b)
breadboards: 2

parts:
  Bauteil1 = Arduino Uno (Rev3)
  R1 = Resistor [tolerance=±5% resistance=220 package=THT]
  LED2 = LED - 5mm [color="Red (633nm)" package="5 mm [THT]"]
  LED3 = LED - 5mm [color="Green (555nm)" package="5 mm [THT]"]
  LED4 = LED - 5mm [color="Blue (430nm)" package="5 mm [THT]"]
  LED5 = LED - 5mm [color="White (6500K)" package="5 mm [THT]"]
  LED6 = LED - 5mm [color="Infrared (880nm)" package="5 mm [THT]"]
  LED1 = smd LED [color="Infrared (880nm)" package="0603 [SMD]"]
  LED7 = LED - 5mm [color="Green (555nm)" package="5 mm [THT]"]

nets:
  N1: Bauteil1.D12/MISO, LED7.cathode
  N2: Bauteil1.GND, R1.Pin_0
  N3: Bauteil1.D2, LED6.anode
  N4: Bauteil1.D3_PWM, LED5.cathode
  N5: Bauteil1.D4, LED4.cathode
  N6: Bauteil1.D5_PWM, LED3.cathode
  N7: Bauteil1.D6_PWM, LED2.cathode
  N8: Bauteil1.D7, LED1.anode
  N9: R1.Pin_1, LED2.anode, LED3.anode, LED4.anode, LED5.anode, LED6.cathode, LED1.cathode, LED7.anode
